# Fritzing sketch ESP32Cam_GateMonitor (bottom) (saved by Fritzing 0.9.3b)

parts:
  Part2 = Adafruit TSL2561 [part_number="Adafruit #439"]
  AM1 = AM312
  ESP32-Cam1 = ESP32-CAM
  FTDI_Programmer1 = FT232RL
  S2 = Reed switch [package=THT]
  DS1 = DS18B20 1-Wire Temperature Sensor [part_number=DS18B20]
  R1 = Resistor [tolerance=±5% resistance=4.7k package=THT]

nets:
  VDD: Part2.VIN, AM1.VDD, ESP32-Cam1.3.3V_/_5V, DS1.VDD, R1.Pin_0
  GND: Part2.GND, AM1.GND, ESP32-Cam1.GND#15, DS1.GND
  N1: Part2.SDA, ESP32-Cam1.CLK
  N2: Part2.SCL, ESP32-Cam1.CMD
  N3: AM1.SIG, ESP32-Cam1.DATA3
  N4: ESP32-Cam1.GND#1, FTDI_Programmer1.GND, S2.pin_2
  N5: ESP32-Cam1.U0TXD, FTDI_Programmer1.RXI
  N6: ESP32-Cam1.U0RXD, FTDI_Programmer1.TXO
  N7: ESP32-Cam1.GND#5, ESP32-Cam1.MCLK
  N8: ESP32-Cam1.DATA0, DS1.DQ, R1.Pin_1
  N9: ESP32-Cam1.DATA2, S2.pin_1
  N10: ESP32-Cam1.5V, FTDI_Programmer1.POWER

notes:
  3.3V
  5V
  ESP32-Cam
  DS18B20
  TSL2561
  AM312
  Reed
  FT232L
  GPIO12
  GPIO2
  GPIO14
  GPIO15
  GPIO13
  4K7

custom parts:
  Adafruit TSL2561: The TSL2561 luminosity sensor is an advanced digital light sensor, ideal for use in a wide range of light situations. Compared to low cost CdS cells, this sensor is more precise, allowing for exact lux calculations and can be configured for different gain/timing ranges to detect light ranges from up to 0.1 - 40,000+ Lux on the fly. The best part of this sensor is that it contains both infrared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
  AM312: AM312 PIR sensor
  FT232RL: Description: This is the newest revision of our FTDI Basic. We now use a SMD 6-pin header on the bottom, which makes it smaller and more compact. Functionality has remained the same. This is a basic breakout board for the FTDI FT232RL USB to serial IC. The pinout of this board matches the FTDI cable to work with official Arduino and cloned 5V Arduino boards. It can also be used for general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
